// Logisim project RiscV32_Part2_Forwarding.circ as structural Verilog: 18 circuits, main circuit main
module main (
);

  wire button_1_out, clock_1_out, cpu_1_illegal, cpu_1_load, cpu_1_store, or_1_out;
  wire [2:0] cpu_1_memwidth;
  wire [31:0] cpu_1_memaddr, cpu_1_pc, cpu_1_storevalue, memory_1_loadvalue, rom_1_data;

  Clock clock_1 (.out(clock_1_out));
  Button button_1 (.out(button_1_out));
  or or_1 (or_1_out, cpu_1_illegal, clock_1_out);
  CPU cpu_1 (
    .Instruction(rom_1_data), .LoadValue(memory_1_loadvalue), .Clock(or_1_out), .Reset(button_1_out),
    .Illegal(cpu_1_illegal), .MemWidth(cpu_1_memwidth), .Store(cpu_1_store), .Load(cpu_1_load),
    .MemAddr(cpu_1_memaddr), .StoreValue(cpu_1_storevalue), .PC(cpu_1_pc));
  ROM #(.addrWidth(24), .dataWidth(32)) rom_1 (.addr(cpu_1_pc[25:2]), .data(rom_1_data));
  Memory memory_1 (
    .Width(cpu_1_memwidth), .Store(cpu_1_store), .Load(cpu_1_load), .Address(cpu_1_memaddr),
    .StoreValue(cpu_1_storevalue), .Clock(or_1_out), .LoadValue(memory_1_loadvalue));

  // Notes on the sheet:
  //   contents of rom_1 (hex, n*v repeats v):
  //   a00093 1400113 1e00193 2800213 102023 202223 302423 402623 2283 402303 802383 c02403 63
endmodule

module Extractor (
  input  [31:0] Instruction,
  input  [2:0] Format,
  output [6:0] Opcode,
  output [4:0] RD,
  output [2:0] Funct3,
  output [4:0] RS1,
  output [4:0] RS2,
  output [6:0] funct7,
  output [31:0] Immediate
);

  Multiplexer #(.select(3), .width(32)) multiplexer_1 (
    .in1({{21{Instruction[31]}}, Instruction[30:20]}),
    .in2({{21{Instruction[31]}}, Instruction[30:25], Instruction[11:7]}),
    .in3({{20{Instruction[31]}}, Instruction[7], Instruction[30:25], Instruction[11:8], 1'b0}),
    .in4({Instruction[31:12], {12{1'b0}}}),
    .in5({{12{Instruction[31]}}, Instruction[19:12], Instruction[20], Instruction[30:21], 1'b0}),
    .in6({32{1'b0}}), .in7({32{1'b0}}), .out(Immediate), .sel(Format));  // open: in0

  assign Funct3 = Instruction[14:12];
  assign funct7 = Instruction[31:25];
  assign Opcode = Instruction[6:0];
  assign RD = Instruction[11:7];
  assign RS1 = Instruction[19:15];
  assign RS2 = Instruction[24:20];

  // Notes on the sheet:
  //   I-type
  //   S-type
  //   B-type
  //   U-type
  //   J-type
endmodule

module Registers16 (
  input  Write,
  input  [3:0] RD,
  input  Clock,
  input  [31:0] Data,
  input  [3:0] RS1,
  input  [3:0] RS2,
  output [31:0] Out1,
  output [31:0] Out2
);

  wire decoder_1_out0, decoder_1_out1, decoder_1_out2, decoder_1_out3, decoder_1_out4, decoder_1_out5,
       decoder_1_out6, decoder_1_out7, decoder_1_out8, decoder_1_out9, decoder_1_out10, decoder_1_out11,
       decoder_1_out12, decoder_1_out13, decoder_1_out14, decoder_1_out15;
  wire [31:0] register_1_q, register_2_q, register_3_q, register_4_q, register_5_q, register_6_q,
       register_7_q, register_8_q, register_9_q, register_10_q, register_11_q, register_12_q, register_13_q,
       register_14_q, register_15_q, register_16_q;

  Multiplexer #(.select(4), .width(32)) multiplexer_1 (
    .in0(register_1_q), .in1(register_2_q), .in2(register_3_q), .in3(register_4_q), .in4(register_5_q),
    .in5(register_6_q), .in6(register_7_q), .in7(register_8_q), .in8(register_9_q), .in9(register_10_q),
    .in10(register_11_q), .in11(register_12_q), .in12(register_13_q), .in13(register_14_q),
    .in14(register_15_q), .in15(register_16_q), .out(Out1), .sel(RS1));
  Multiplexer #(.select(4), .width(32)) multiplexer_2 (
    .in0(register_1_q), .in1(register_2_q), .in2(register_3_q), .in3(register_4_q), .in4(register_5_q),
    .in5(register_6_q), .in6(register_7_q), .in7(register_8_q), .in8(register_9_q), .in9(register_10_q),
    .in10(register_11_q), .in11(register_12_q), .in12(register_13_q), .in13(register_14_q),
    .in14(register_15_q), .in15(register_16_q), .out(Out2), .sel(RS2));
  Decoder #(.select(4)) decoder_1 (
    .out0(decoder_1_out0), .out1(decoder_1_out1), .out2(decoder_1_out2), .out3(decoder_1_out3),
    .out4(decoder_1_out4), .out5(decoder_1_out5), .out6(decoder_1_out6), .out7(decoder_1_out7),
    .out8(decoder_1_out8), .out9(decoder_1_out9), .out10(decoder_1_out10), .out11(decoder_1_out11),
    .out12(decoder_1_out12), .out13(decoder_1_out13), .out14(decoder_1_out14), .out15(decoder_1_out15),
    .sel(RD), .en(Write));
  Register #(.trigger("falling"), .width(32)) register_1 (
    .D(Data), .en(decoder_1_out0), .clk(Clock), .Q(register_1_q));  // open: clr
  Register #(.trigger("falling"), .width(32)) register_2 (
    .D(Data), .en(decoder_1_out1), .clk(Clock), .Q(register_2_q));  // open: clr
  Register #(.trigger("falling"), .width(32)) register_3 (
    .D(Data), .en(decoder_1_out2), .clk(Clock), .Q(register_3_q));  // open: clr
  Register #(.trigger("falling"), .width(32)) register_4 (
    .D(Data), .en(decoder_1_out3), .clk(Clock), .Q(register_4_q));  // open: clr
  Register #(.trigger("falling"), .width(32)) register_5 (
    .D(Data), .en(decoder_1_out4), .clk(Clock), .Q(register_5_q));  // open: clr
  Register #(.trigger("falling"), .width(32)) register_6 (
    .D(Data), .en(decoder_1_out5), .clk(Clock), .Q(register_6_q));  // open: clr
  Register #(.trigger("falling"), .width(32)) register_7 (
    .D(Data), .en(decoder_1_out6), .clk(Clock), .Q(register_7_q));  // open: clr
  Register #(.trigger("falling"), .width(32)) register_8 (
    .D(Data), .en(decoder_1_out7), .clk(Clock), .Q(register_8_q));  // open: clr
  Register #(.trigger("falling"), .width(32)) register_9 (
    .D(Data), .en(decoder_1_out8), .clk(Clock), .Q(register_9_q));  // open: clr
  Register #(.trigger("falling"), .width(32)) register_10 (
    .D(Data), .en(decoder_1_out9), .clk(Clock), .Q(register_10_q));  // open: clr
  Register #(.trigger("falling"), .width(32)) register_11 (
    .D(Data), .en(decoder_1_out10), .clk(Clock), .Q(register_11_q));  // open: clr
  Register #(.trigger("falling"), .width(32)) register_12 (
    .D(Data), .en(decoder_1_out11), .clk(Clock), .Q(register_12_q));  // open: clr
  Register #(.trigger("falling"), .width(32)) register_13 (
    .D(Data), .en(decoder_1_out12), .clk(Clock), .Q(register_13_q));  // open: clr
  Register #(.trigger("falling"), .width(32)) register_14 (
    .D(Data), .en(decoder_1_out13), .clk(Clock), .Q(register_14_q));  // open: clr
  Register #(.trigger("falling"), .width(32)) register_15 (
    .D(Data), .en(decoder_1_out14), .clk(Clock), .Q(register_15_q));  // open: clr
  Register #(.trigger("falling"), .width(32)) register_16 (
    .D(Data), .en(decoder_1_out15), .clk(Clock), .Q(register_16_q));  // open: clr
endmodule

module Registers16WithZero (
  input  Write,
  input  [3:0] RD,
  input  Clock,
  input  [31:0] Data,
  input  [3:0] RS1,
  input  [3:0] RS2,
  output [31:0] Out1,
  output [31:0] Out2
);

  wire decoder_1_out1, decoder_1_out2, decoder_1_out3, decoder_1_out4, decoder_1_out5, decoder_1_out6,
       decoder_1_out7, decoder_1_out8, decoder_1_out9, decoder_1_out10, decoder_1_out11, decoder_1_out12,
       decoder_1_out13, decoder_1_out14, decoder_1_out15;
  wire [31:0] register_1_q, register_2_q, register_3_q, register_4_q, register_5_q, register_6_q,
       register_7_q, register_8_q, register_9_q, register_10_q, register_11_q, register_12_q, register_13_q,
       register_14_q, register_15_q;

  Multiplexer #(.select(4), .width(32)) multiplexer_1 (
    .in0({32{1'b0}}), .in1(register_1_q), .in2(register_2_q), .in3(register_3_q), .in4(register_4_q),
    .in5(register_5_q), .in6(register_6_q), .in7(register_7_q), .in8(register_8_q), .in9(register_9_q),
    .in10(register_10_q), .in11(register_11_q), .in12(register_12_q), .in13(register_13_q),
    .in14(register_14_q), .in15(register_15_q), .out(Out1), .sel(RS1));
  Multiplexer #(.select(4), .width(32)) multiplexer_2 (
    .in0({32{1'b0}}), .in1(register_1_q), .in2(register_2_q), .in3(register_3_q), .in4(register_4_q),
    .in5(register_5_q), .in6(register_6_q), .in7(register_7_q), .in8(register_8_q), .in9(register_9_q),
    .in10(register_10_q), .in11(register_11_q), .in12(register_12_q), .in13(register_13_q),
    .in14(register_14_q), .in15(register_15_q), .out(Out2), .sel(RS2));
  Decoder #(.select(4)) decoder_1 (
    .out1(decoder_1_out1), .out2(decoder_1_out2), .out3(decoder_1_out3), .out4(decoder_1_out4),
    .out5(decoder_1_out5), .out6(decoder_1_out6), .out7(decoder_1_out7), .out8(decoder_1_out8),
    .out9(decoder_1_out9), .out10(decoder_1_out10), .out11(decoder_1_out11), .out12(decoder_1_out12),
    .out13(decoder_1_out13), .out14(decoder_1_out14), .out15(decoder_1_out15), .sel(RD), .en(Write));  // open: out0
  Register #(.trigger("falling"), .width(32)) register_1 (
    .D(Data), .en(decoder_1_out1), .clk(Clock), .Q(register_1_q));  // open: clr
  Register #(.trigger("falling"), .width(32)) register_2 (
    .D(Data), .en(decoder_1_out2), .clk(Clock), .Q(register_2_q));  // open: clr
  Register #(.trigger("falling"), .width(32)) register_3 (
    .D(Data), .en(decoder_1_out3), .clk(Clock), .Q(register_3_q));  // open: clr
  Register #(.trigger("falling"), .width(32)) register_4 (
    .D(Data), .en(decoder_1_out4), .clk(Clock), .Q(register_4_q));  // open: clr
  Register #(.trigger("falling"), .width(32)) register_5 (
    .D(Data), .en(decoder_1_out5), .clk(Clock), .Q(register_5_q));  // open: clr
  Register #(.trigger("falling"), .width(32)) register_6 (
    .D(Data), .en(decoder_1_out6), .clk(Clock), .Q(register_6_q));  // open: clr
  Register #(.trigger("falling"), .width(32)) register_7 (
    .D(Data), .en(decoder_1_out7), .clk(Clock), .Q(register_7_q));  // open: clr
  Register #(.trigger("falling"), .width(32)) register_8 (
    .D(Data), .en(decoder_1_out8), .clk(Clock), .Q(register_8_q));  // open: clr
  Register #(.trigger("falling"), .width(32)) register_9 (
    .D(Data), .en(decoder_1_out9), .clk(Clock), .Q(register_9_q));  // open: clr
  Register #(.trigger("falling"), .width(32)) register_10 (
    .D(Data), .en(decoder_1_out10), .clk(Clock), .Q(register_10_q));  // open: clr
  Register #(.trigger("falling"), .width(32)) register_11 (
    .D(Data), .en(decoder_1_out11), .clk(Clock), .Q(register_11_q));  // open: clr
  Register #(.trigger("falling"), .width(32)) register_12 (
    .D(Data), .en(decoder_1_out12), .clk(Clock), .Q(register_12_q));  // open: clr
  Register #(.trigger("falling"), .width(32)) register_13 (
    .D(Data), .en(decoder_1_out13), .clk(Clock), .Q(register_13_q));  // open: clr
  Register #(.trigger("falling"), .width(32)) register_14 (
    .D(Data), .en(decoder_1_out14), .clk(Clock), .Q(register_14_q));  // open: clr
  Register #(.trigger("falling"), .width(32)) register_15 (
    .D(Data), .en(decoder_1_out15), .clk(Clock), .Q(register_15_q));  // open: clr

  // Notes on the sheet:
  //   ZERO
  //   RA
  //   SP
  //   GP
  //   TP
  //   T0
  //   T1
  //   T2
  //   S0
  //   S1
  //   A0
  //   A1
  //   S2
  //   S3
  //   S4
  //   S5
endmodule

module RegisterFile (
  input  [31:0] Data,
  input  [4:0] RD,
  input  Write,
  input  Clock,
  input  [4:0] RS1,
  input  [4:0] RS2,
  output [31:0] Out1,
  output [31:0] Out2
);

  wire demultiplexer_1_out0, demultiplexer_1_out1;
  wire [31:0] BottomRegisters_out1, BottomRegisters_out2, TopRegisters_out1, TopRegisters_out2;

  Demultiplexer demultiplexer_1 (.out0(demultiplexer_1_out0), .out1(demultiplexer_1_out1), .in(Write), .sel(RD[4]));
  Registers16WithZero BottomRegisters (
    .Write(demultiplexer_1_out0), .RD(RD[3:0]), .Clock(Clock), .Data(Data), .RS1(RS1[3:0]), .RS2(RS2[3:0]),
    .Out1(BottomRegisters_out1), .Out2(BottomRegisters_out2));
  Registers16 TopRegisters (
    .Write(demultiplexer_1_out1), .RD(RD[3:0]), .Clock(Clock), .Data(Data), .RS1(RS1[3:0]), .RS2(RS2[3:0]),
    .Out1(TopRegisters_out1), .Out2(TopRegisters_out2));
  Multiplexer #(.width(32)) multiplexer_1 (
    .in0(BottomRegisters_out1), .in1(TopRegisters_out1), .out(Out1), .sel(RS1[4]));
  Multiplexer #(.width(32)) multiplexer_2 (
    .in0(BottomRegisters_out2), .in1(TopRegisters_out2), .out(Out2), .sel(RS2[4]));
endmodule

module CPU (
  input  [31:0] Instruction,
  input  [31:0] LoadValue,
  input  Clock,
  input  Reset,
  output Illegal,
  output [2:0] MemWidth,
  output Store,
  output Load,
  output [31:0] MemAddr,
  output [31:0] StoreValue,
  output [31:0] PC
);

  wire and_1_out, and_3_out, branchunit_1_branch, d_ff_1_q, d_ff_2_q, d_ff_3_q, decoder_1_out0,
       decoder_1_out3, decoder_1_out4, decoder_1_out5, decoder_1_out8, decoder_1_out12, decoder_1_out13,
       decoder_1_out24, decoder_1_out25, decoder_1_out27, ex_mem_register_control_1_aluresult_enable_out,
       ex_mem_register_control_1_auipc_out, ex_mem_register_control_1_immediate_enab_out,
       ex_mem_register_control_1_storepc_out, ex_mem_register_control_1_write_out,
       id_ex_register_control_1_aluresult_enable_out, id_ex_register_control_1_alusrc_out,
       id_ex_register_control_1_auipc_out, id_ex_register_control_1_immediate_enab_out,
       id_ex_register_control_1_load_out, id_ex_register_control_1_pcsrc_out,
       id_ex_register_control_1_rjump1_out, id_ex_register_control_1_rjump2_out,
       id_ex_register_control_1_store_out, id_ex_register_control_1_storepc_out,
       id_ex_register_control_1_write_out, mem_wb_register_control_1_aluresult_enable_out,
       mem_wb_register_control_1_auipc_out, mem_wb_register_control_1_immediate_enab_out,
       mem_wb_register_control_1_load_out, mem_wb_register_control_1_storepc_out,
       mem_wb_register_control_1_write_out, nand_1_out, nor_1_out, not_2_out, or_1_out, or_2_out, or_6_out,
       or_7_out, priority_encoder_1_p2, priority_encoder_1_p6, priority_encoder_1_p7, shift_register_1_p2,
       shift_register_1_p3, shift_register_1_p10, shift_register_1_p11, shift_register_1_p12,
       shift_register_1_p13;
  wire [1:0] extractor_1_opcode;
  wire [2:0] extractor_1_funct3, id_ex_register_data_1_funct3_out, priority_encoder_1_p5;
  wire [4:0] ex_mem_register_data_1_rd_out, extractor_1_opcode_2, extractor_1_rd, extractor_1_rs1,
       extractor_1_rs2, id_ex_data_1_rs1_out, id_ex_data_1_rs2_out, id_ex_register_data_1_rd_out,
       mem_wb_register_data_1_rd_out;
  wire [6:0] extractor_1_funct7, id_ex_register_data_1_funct7_out;
  wire [31:0] adder_1_out, adder_2_out, adder_3_out, adder_4_out, adder_5_out, alu_1_data,
       controlled_buffer_1_out, ex_mem_register_data_1_aluresult_out,
       ex_mem_register_data_1_auipc_result_out, ex_mem_register_data_1_immediate_out,
       ex_mem_register_data_1_pcplus4_out, extractor_1_immediate, forwarding_unit_1_a, forwarding_unit_1_b,
       id_ex_register_data_1_immediate_out, id_ex_register_data_1_out1_out, id_ex_register_data_1_out2_out,
       id_ex_register_data_1_pc_out, id_ex_register_data_1_pcplus4_out, if_id_register_1_instruction_out,
       if_id_register_1_pc_out, if_id_register_1_pcplus4_out, mem_wb_register_data_1_aluresult_out,
       mem_wb_register_data_1_auipc_result_out, mem_wb_register_data_1_immediate_out,
       mem_wb_register_data_1_loadvalue_out, mem_wb_register_data_1_pcpluse4_out, multiplexer_1_out,
       multiplexer_2_out, multiplexer_3_out, multiplexer_4_out, registerfile_1_out1, registerfile_1_out2;

  D_Flip_Flop d_ff_1 (.D(1'b1), .clk(Clock), .Q(d_ff_1_q), .reset(Reset));  // open: Qn, preset
  // Shift_Register #(.length(4)) shift_register_1: pin names not known; wires that end beside it: Reset, shift_register_1_p2, shift_register_1_p3, Clock, shift_register_1_p2, shift_register_1_p2, shift_register_1_p2, shift_register_1_p2, shift_register_1_p2, shift_register_1_p10, shift_register_1_p11, shift_register_1_p12, shift_register_1_p13
  not not_1 (shift_register_1_p3, shift_register_1_p2);
  D_Flip_Flop d_ff_2 (.D(d_ff_1_q), .clk(Clock), .Q(d_ff_2_q), .reset(Reset));  // open: Qn, preset
  IF_ID_Register if_id_register_1 (
    .Instruction_in(Instruction), .PC_in(PC), .PCPlus4_in(adder_3_out), .Flush(shift_register_1_p2),
    .Clock(Clock), .Rest(Reset), .Instruction_out(if_id_register_1_instruction_out),
    .PC_out(if_id_register_1_pc_out), .PCPlus4_out(if_id_register_1_pcplus4_out));
  nor nor_1 (nor_1_out, shift_register_1_p10, shift_register_1_p11, shift_register_1_p12, shift_register_1_p13);
  D_Flip_Flop d_ff_3 (.D(and_1_out), .clk(Clock), .Q(d_ff_3_q), .reset(Reset));  // open: Qn, preset
  and and_1 (and_1_out, d_ff_2_q, or_1_out);
  and and_2 (Illegal, nor_1_out, d_ff_3_q);
  Decoder #(.select(5)) decoder_1 (
    .out0(decoder_1_out0), .out3(decoder_1_out3), .out4(decoder_1_out4), .out5(decoder_1_out5),
    .out8(decoder_1_out8), .out12(decoder_1_out12), .out13(decoder_1_out13), .out24(decoder_1_out24),
    .out25(decoder_1_out25), .out27(decoder_1_out27), .sel(extractor_1_opcode_2));  // open: out1, out2, out6, out7, out9, out10, out11, out14, out15, out16, out17, out18, out19, out20, out21, out22, out23, out26, out28, out29, out30, out31, en
  Extractor extractor_1 (
    .Instruction(if_id_register_1_instruction_out), .Format(priority_encoder_1_p5),
    .Opcode({extractor_1_opcode_2, extractor_1_opcode}), .RD(extractor_1_rd), .Funct3(extractor_1_funct3),
    .RS1(extractor_1_rs1), .RS2(extractor_1_rs2), .funct7(extractor_1_funct7),
    .Immediate(extractor_1_immediate));
  Register #(.trigger("falling"), .width(32)) register_1 (
    .D(multiplexer_2_out), .clk(Clock), .Q(PC), .clr(Reset));  // open: en
  Multiplexer #(.width(32)) multiplexer_1 (
    .in0(PC), .in1(id_ex_register_data_1_pc_out), .out(multiplexer_1_out), .sel(shift_register_1_p2));
  nand nand_1 (nand_1_out, extractor_1_opcode[1], extractor_1_opcode[0]);
  assign controlled_buffer_1_out = mem_wb_register_control_1_auipc_out ? mem_wb_register_data_1_auipc_result_out : 32'bz;  // Controlled_Buffer controlled_buffer_1
  Adder #(.width(32)) adder_1 (
    .a(id_ex_register_data_1_pc_out), .b(id_ex_register_data_1_immediate_out), .out(adder_1_out));  // open: cin, cout
  Multiplexer #(.width(32)) multiplexer_2 (
    .in0(adder_2_out), .in1(adder_4_out), .out(multiplexer_2_out), .sel(id_ex_register_control_1_pcsrc_out));
  Adder #(.width(32)) adder_2 (.a(multiplexer_1_out), .b(multiplexer_3_out), .out(adder_2_out));  // open: cin, cout
  assign controlled_buffer_1_out = mem_wb_register_control_1_storepc_out ? mem_wb_register_data_1_pcpluse4_out : 32'bz;  // Controlled_Buffer controlled_buffer_2
  Adder #(.width(32)) adder_3 (.a(PC), .b(32'h4), .out(adder_3_out));  // open: cin, cout
  or or_1 (or_1_out, nand_1_out, not_2_out);
  not not_2 (not_2_out, priority_encoder_1_p7);
  Multiplexer #(.width(32)) multiplexer_3 (
    .in0(32'h4), .in1(id_ex_register_data_1_immediate_out), .out(multiplexer_3_out), .sel(shift_register_1_p2));
  RegisterFile registerfile_1 (
    .Data(controlled_buffer_1_out), .RD(mem_wb_register_data_1_rd_out),
    .Write(mem_wb_register_control_1_write_out), .Clock(Clock), .RS1(id_ex_data_1_rs1_out),
    .RS2(id_ex_data_1_rs2_out), .Out1(registerfile_1_out1), .Out2(registerfile_1_out2));
  ID_EX_Data id_ex_data_1 (
    .RS1_in(extractor_1_rs1), .RS2_in(extractor_1_rs2), .Clock(Clock), .Rest(Reset),
    .RS1_out(id_ex_data_1_rs1_out), .RS2_out(id_ex_data_1_rs2_out));
  ID_EX_Register_Data id_ex_register_data_1 (
    .Out1_in(registerfile_1_out1), .Out2_in(registerfile_1_out2), .immediate_in(extractor_1_immediate),
    .PC_in(if_id_register_1_pc_out), .Funct3_in(extractor_1_funct3), .Funct7_in(extractor_1_funct7),
    .RD_in(extractor_1_rd), .PCPlus4_in(if_id_register_1_pcplus4_out), .Rest(Reset), .Clock(Clock),
    .Out1_out(id_ex_register_data_1_out1_out), .Out2_out(id_ex_register_data_1_out2_out),
    .immediate_out(id_ex_register_data_1_immediate_out), .PC_out(id_ex_register_data_1_pc_out),
    .Funct3_out(id_ex_register_data_1_funct3_out), .Funct7_out(id_ex_register_data_1_funct7_out),
    .RD_out(id_ex_register_data_1_rd_out), .PCPlus4_out(id_ex_register_data_1_pcplus4_out));
  ID_EX_Register_Control id_ex_register_control_1 (
    .Load_in(decoder_1_out0), .Store_in(decoder_1_out8), .ALUResult_Enable_in(or_7_out), .Write_in(or_6_out),
    .immediate_Enable_in(decoder_1_out13), .ALUSrc_in(decoder_1_out4), .AUIPC_in(decoder_1_out5),
    .RJump1_in(decoder_1_out24), .RJump2_in(decoder_1_out27), .StorePC_in(or_2_out),
    .PCSrc_in(decoder_1_out25), .Rest(Reset), .Clock(Clock), .Flush(shift_register_1_p2),
    .Load_out(id_ex_register_control_1_load_out), .Store_out(id_ex_register_control_1_store_out),
    .ALUResult_Enable_out(id_ex_register_control_1_aluresult_enable_out),
    .Write_out(id_ex_register_control_1_write_out),
    .immediate_Enab_out(id_ex_register_control_1_immediate_enab_out),
    .ALUSrc_out(id_ex_register_control_1_alusrc_out), .AUIPC_out(id_ex_register_control_1_auipc_out),
    .RJump1_out(id_ex_register_control_1_rjump1_out), .RJump2_out(id_ex_register_control_1_rjump2_out),
    .StorePC_out(id_ex_register_control_1_storepc_out), .PCSrc_out(id_ex_register_control_1_pcsrc_out));
  Forwarding_Unit forwarding_unit_1 (
    .Rs1(id_ex_data_1_rs1_out), .Out1_in(id_ex_register_data_1_out1_out),
    .EXMEM_RD(ex_mem_register_data_1_rd_out), .EXMEM_Write(ex_mem_register_control_1_write_out),
    .MEMWB_RD(mem_wb_register_data_1_rd_out), .MEMWB_Write(mem_wb_register_control_1_write_out),
    .Rs2(id_ex_data_1_rs2_out), .Out2_in(id_ex_register_data_1_out2_out),
    .EXMEM_Result(ex_mem_register_data_1_aluresult_out), .MEMWB_Result(controlled_buffer_1_out),
    .A(forwarding_unit_1_a), .B(forwarding_unit_1_b));
  // Priority_Encoder priority_encoder_1: pin names not known; wires that end beside it: decoder_1_out12, priority_encoder_1_p2, decoder_1_out8, decoder_1_out24, priority_encoder_1_p5, priority_encoder_1_p6, priority_encoder_1_p7, decoder_1_out27, 1'b0, 1'b0
  Multiplexer #(.width(32)) multiplexer_4 (
    .in0(forwarding_unit_1_b), .in1(id_ex_register_data_1_immediate_out), .out(multiplexer_4_out),
    .sel(id_ex_register_control_1_alusrc_out));
  assign controlled_buffer_1_out = mem_wb_register_control_1_immediate_enab_out ? mem_wb_register_data_1_immediate_out : 32'bz;  // Controlled_Buffer controlled_buffer_3
  or or_2 (or_2_out, decoder_1_out27, decoder_1_out25);
  or or_3 (priority_encoder_1_p6, decoder_1_out13, decoder_1_out5);
  or or_4 (priority_encoder_1_p2, decoder_1_out3, decoder_1_out4, decoder_1_out0, decoder_1_out25);
  and and_3 (and_3_out, branchunit_1_branch, id_ex_register_control_1_rjump1_out);
  or or_5 (shift_register_1_p2, and_3_out, id_ex_register_control_1_rjump2_out);
  or or_6 (or_6_out, decoder_1_out25, decoder_1_out12, decoder_1_out4, decoder_1_out0, decoder_1_out5, decoder_1_out13, decoder_1_out27);
  Adder #(.width(32)) adder_4 (
    .a(forwarding_unit_1_a), .b(id_ex_register_data_1_immediate_out), .out(adder_4_out));  // open: cin, cout
  or or_7 (or_7_out, decoder_1_out12, decoder_1_out4);
  ALU alu_1 (
    .A(forwarding_unit_1_a), .B(multiplexer_4_out), .Funct3(id_ex_register_data_1_funct3_out),
    .funct7(id_ex_register_data_1_funct7_out), .Imm(id_ex_register_control_1_alusrc_out), .Data(alu_1_data));
  BranchUnit branchunit_1 (
    .A(forwarding_unit_1_a), .B(multiplexer_4_out), .Funct3(id_ex_register_data_1_funct3_out),
    .Branch(branchunit_1_branch));
  assign controlled_buffer_1_out = mem_wb_register_control_1_aluresult_enable_out ? mem_wb_register_data_1_aluresult_out : 32'bz;  // Controlled_Buffer controlled_buffer_4
  EX_MEM_Register_Data ex_mem_register_data_1 (
    .MemWidth_in(id_ex_register_data_1_funct3_out), .immediate_in(id_ex_register_data_1_immediate_out),
    .MemAddr_in(adder_5_out), .StoreValue_in(multiplexer_4_out), .ALUResult_in(alu_1_data),
    .PCPlus4_in(id_ex_register_data_1_pcplus4_out), .AUIPC_Result_in(adder_1_out),
    .RD_in(id_ex_register_data_1_rd_out), .Clock(Clock), .Rest(Reset), .MemWidth_out(MemWidth),
    .immediate_out(ex_mem_register_data_1_immediate_out), .MemAddr_out(MemAddr), .StoreValue_out(StoreValue),
    .ALUResult_out(ex_mem_register_data_1_aluresult_out), .PCPlus4_out(ex_mem_register_data_1_pcplus4_out),
    .AUIPC_Result_out(ex_mem_register_data_1_auipc_result_out), .RD_out(ex_mem_register_data_1_rd_out));
  EX_MEM_Register_Control ex_mem_register_control_1 (
    .Store_in(id_ex_register_control_1_store_out), .Load_in(id_ex_register_control_1_load_out),
    .ALUResult_Enable_in(id_ex_register_control_1_aluresult_enable_out),
    .AUIPC_in(id_ex_register_control_1_auipc_out), .StorePC_in(id_ex_register_control_1_storepc_out),
    .Write_in(id_ex_register_control_1_write_out),
    .immediate_Enable_in(id_ex_register_control_1_immediate_enab_out), .Clock(Clock), .Rest(Reset),
    .Store_out(Store), .Load_out(Load),
    .ALUResult_Enable_out(ex_mem_register_control_1_aluresult_enable_out),
    .AUIPC_out(ex_mem_register_control_1_auipc_out), .StorePC_out(ex_mem_register_control_1_storepc_out),
    .Write_out(ex_mem_register_control_1_write_out),
    .immediate_Enab_out(ex_mem_register_control_1_immediate_enab_out));
  assign controlled_buffer_1_out = mem_wb_register_control_1_load_out ? mem_wb_register_data_1_loadvalue_out : 32'bz;  // Controlled_Buffer controlled_buffer_5
  Adder #(.width(32)) adder_5 (
    .a(forwarding_unit_1_a), .b(id_ex_register_data_1_immediate_out), .out(adder_5_out));  // open: cin, cout
  MEM_WB_Register_Data mem_wb_register_data_1 (
    .LoadValue_in(LoadValue), .RD_in(ex_mem_register_data_1_rd_out),
    .immediate_in(ex_mem_register_data_1_immediate_out), .ALUResult_in(ex_mem_register_data_1_aluresult_out),
    .PCPluse4_in(ex_mem_register_data_1_pcplus4_out),
    .AUIPC_Result_in(ex_mem_register_data_1_auipc_result_out), .Rest(Reset), .Clock(Clock),
    .LoadValue_out(mem_wb_register_data_1_loadvalue_out), .RD_out(mem_wb_register_data_1_rd_out),
    .immediate_out(mem_wb_register_data_1_immediate_out),
    .ALUResult_out(mem_wb_register_data_1_aluresult_out), .PCPluse4_out(mem_wb_register_data_1_pcpluse4_out),
    .AUIPC_Result_out(mem_wb_register_data_1_auipc_result_out));
  MEM_WB_Register_Control mem_wb_register_control_1 (
    .ALUResult_Enable_in(ex_mem_register_control_1_aluresult_enable_out),
    .Write_in(ex_mem_register_control_1_write_out),
    .immediate_Enab_in(ex_mem_register_control_1_immediate_enab_out),
    .AUIPC_in(ex_mem_register_control_1_auipc_out), .Load_in(Load),
    .StorePC_in(ex_mem_register_control_1_storepc_out), .Clock(Clock), .Rest(Reset),
    .ALUResult_Enable_out(mem_wb_register_control_1_aluresult_enable_out),
    .Write_out(mem_wb_register_control_1_write_out),
    .immediate_Enab_out(mem_wb_register_control_1_immediate_enab_out),
    .AUIPC_out(mem_wb_register_control_1_auipc_out), .Load_out(mem_wb_register_control_1_load_out),
    .StorePc_out(mem_wb_register_control_1_storepc_out));

  // Notes on the sheet:
  //   Instruction: initial=0x33
  //   PCsrc
  //   AUIPC_Result
  //   AUIPC
  //   PCPlus4
  //   Relative Jump?
  //   Store PC?
  //   Write
  //   ALUSrc
  //   JALR
  //   RJump1
  //   RJump2
  //   ALUResult_Enable
  //   immediate_Enabe
  //   A
  //   Imm
endmodule

module ALU (
  input  [31:0] A,
  input  [31:0] B,
  input  [2:0] Funct3,
  input  [6:0] funct7,
  input  Imm,
  output [31:0] Data
);

  wire and_2_out, and_3_out, not_1_out;
  wire [0:0] comparator_1_lt, comparator_2_lt;
  wire [31:0] adder_1_out, and_1_out, divider_1_out, divider_1_rem, divider_2_out, divider_2_rem,
       multiplexer_1_out, multiplexer_2_out, multiplexer_3_out, multiplexer_4_out, multiplexer_6_out,
       negator_1_out, or_1_out, shifter_1_out, shifter_2_out, shifter_3_out, subtractor_1_out, xor_1_out;
  wire [63:0] multiplier_1_out, multiplier_2_out, multiplier_3_out, negator_2_out;

  not not_1 (not_1_out, Imm);
  assign xor_1_out = A ^ B;  // XOR_Gate xor_1, 32 bits wide
  assign or_1_out = A | B;  // OR_Gate or_1, 32 bits wide
  assign and_1_out = A & B;  // AND_Gate and_1, 32 bits wide
  Shifter #(.width(32)) shifter_1 (.in(A), .\dist (B[4:0]), .out(shifter_1_out));
  Shifter #(.shift("lr"), .width(32)) shifter_2 (.in(A), .\dist (B[4:0]), .out(shifter_2_out));
  Shifter #(.shift("ar"), .width(32)) shifter_3 (.in(A), .\dist (B[4:0]), .out(shifter_3_out));
  Negator #(.width(32)) negator_1 (.in(B), .out(negator_1_out));
  Adder #(.width(32)) adder_1 (.a(A), .b(B), .out(adder_1_out));  // open: cin, cout
  Subtractor #(.width(32)) subtractor_1 (.a(A), .b(B), .out(subtractor_1_out));  // open: bin, bout
  and and_2 (and_2_out, funct7[5], not_1_out);
  Comparator #(.width(32)) comparator_1 (.a(A), .b(B), .lt(comparator_1_lt[0]));  // open: gt, eq
  Comparator #(.mode("unsigned"), .width(32)) comparator_2 (.a(A), .b(B), .lt(comparator_2_lt[0]));  // open: gt, eq
  Multiplexer #(.width(32)) multiplexer_1 (
    .in0(shifter_2_out), .in1(shifter_3_out), .out(multiplexer_1_out), .sel(funct7[5]));
  Multiplexer #(.width(32)) multiplexer_2 (
    .in0(adder_1_out), .in1(subtractor_1_out), .out(multiplexer_2_out), .sel(and_2_out));
  Divider #(.width(32)) divider_1 (.a(A), .b(B), .out(divider_1_out), .rem(divider_1_rem));  // open: upper
  Divider #(.mode("twosComplement"), .width(32)) divider_2 (
    .a(A), .b(B), .out(divider_2_out), .rem(divider_2_rem));  // open: upper
  Multiplexer #(.select(3), .width(32)) multiplexer_3 (
    .in0(multiplier_3_out[31:0]), .in1(multiplier_3_out[63:32]), .in2(multiplexer_6_out),
    .in3(multiplier_2_out[63:32]), .in4(divider_2_out), .in5(divider_1_out), .in6(divider_2_rem),
    .in7(divider_1_rem), .out(multiplexer_3_out), .sel(Funct3));
  Multiplexer #(.select(3), .width(32)) multiplexer_4 (
    .in0(multiplexer_2_out), .in1(shifter_1_out), .in2({{31{1'b0}}, comparator_1_lt[0]}),
    .in3({{31{1'b0}}, comparator_2_lt[0]}), .in4(xor_1_out), .in5(multiplexer_1_out), .in6(or_1_out),
    .in7(and_1_out), .out(multiplexer_4_out), .sel(Funct3));
  Multiplier #(.width(64)) multiplier_1 (
    .a({{32{1'b0}}, negator_1_out}), .b({{32{1'b0}}, A}), .out(multiplier_1_out));  // open: cin, cout
  Multiplexer #(.width(32)) multiplexer_5 (
    .in0(multiplexer_4_out), .in1(multiplexer_3_out), .out(Data), .sel(and_3_out));
  and and_3 (and_3_out, funct7[0], ~Imm);  // AND_Gate
  Negator #(.width(64)) negator_2 (.in(multiplier_1_out), .out(negator_2_out));
  Multiplier #(.width(64)) multiplier_2 (
    .a({{32{1'b0}}, B}), .b({{32{1'b0}}, A}), .out(multiplier_2_out));  // open: cin, cout
  Multiplexer #(.width(32)) multiplexer_6 (
    .in0(negator_2_out[63:32]), .in1(multiplier_2_out[63:32]), .out(multiplexer_6_out),
    .sel(negator_1_out[31]));
  Multiplier #(.mode("twosComplement"), .width(64)) multiplier_3 (
    .a({{33{B[31]}}, B[30:0]}), .b({{33{A[31]}}, A[30:0]}), .out(multiplier_3_out));  // open: cin, cout
endmodule

module BranchUnit (
  input  [31:0] A,
  input  [31:0] B,
  input  [2:0] Funct3,
  output Branch
);

  wire comparator_1_eq, comparator_1_gt, comparator_1_lt, comparator_2_eq, comparator_2_gt, comparator_2_lt,
       not_1_out, or_1_out, or_2_out;

  Comparator #(.mode("unsigned"), .width(32)) comparator_1 (
    .a(A), .b(B), .gt(comparator_1_gt), .eq(comparator_1_eq), .lt(comparator_1_lt));
  Comparator #(.width(32)) comparator_2 (
    .a(A), .b(B), .gt(comparator_2_gt), .eq(comparator_2_eq), .lt(comparator_2_lt));
  not not_1 (not_1_out, comparator_1_eq);
  or or_1 (or_1_out, comparator_1_gt, comparator_1_eq);
  or or_2 (or_2_out, comparator_2_gt, comparator_2_eq);
  Multiplexer #(.select(3)) multiplexer_1 (
    .in0(comparator_1_eq), .in1(not_1_out), .in2(1'b0), .in3(1'b0), .in4(comparator_2_lt), .in5(or_2_out),
    .in6(comparator_1_lt), .in7(or_1_out), .out(Branch), .sel(Funct3));
endmodule

module Memory (
  input  [2:0] Width,
  input  Store,
  input  Load,
  input  [31:0] Address,
  input  [31:0] StoreValue,
  input  Clock,
  output [31:0] LoadValue
);

  wire not_1_out, not_2_out, not_3_out, not_4_out, or_1_out;
  wire [1:0] subtractor_1_out_2;
  wire [31:0] multiplexer_1_out, multiplexer_2_out, multiplexer_3_out, multiplexer_4_out, multiplexer_5_out,
       multiplexer_7_out, multiplexer_8_out, multiplexer_9_out, multiplexer_10_out, multiplexer_11_out,
       multiplexer_12_out, ram_1_dout, ram_1_dout_2;
  wire [31:2] subtractor_1_out;
  wire [31:8] ram_1_dout_3, ram_1_dout_4;

  Subtractor #(.width(32)) subtractor_1 (
    .a(Address), .b(32'h1000000), .out({subtractor_1_out, subtractor_1_out_2}));  // open: bin, bout
  or or_1 (or_1_out, Store, Load);
  Multiplexer #(.width(32)) multiplexer_1 (
    .in0({ram_1_dout_4[31], ram_1_dout_4[14:8], ram_1_dout_3[31], ram_1_dout_3[14:8], StoreValue[15:0]}),
    .in1({ram_1_dout_4[31], ram_1_dout_4[14:8], StoreValue[15:0], ram_1_dout[31], ram_1_dout[6:0]}),
    .out(multiplexer_1_out), .sel(subtractor_1_out_2[0]));
  Multiplexer #(.width(32)) multiplexer_2 (
    .in0(multiplexer_1_out),
    .in1({StoreValue[15:0], ram_1_dout_2[31], ram_1_dout_2[6:0], ram_1_dout[31], ram_1_dout[6:0]}),
    .out(multiplexer_2_out), .sel(subtractor_1_out_2[1]));
  Multiplexer #(.select(2), .width(32)) multiplexer_3 (
    .in0({ram_1_dout_4[31], ram_1_dout_4[14:8], ram_1_dout_3[31], ram_1_dout_3[14:8], ram_1_dout_2[31], ram_1_dout_2[6:0], StoreValue[7:0]}),
    .in1({ram_1_dout_4[31], ram_1_dout_4[14:8], ram_1_dout_3[31], ram_1_dout_3[14:8], StoreValue[7:0], ram_1_dout[31], ram_1_dout[6:0]}),
    .in2({ram_1_dout_4[31], ram_1_dout_4[14:8], StoreValue[7:0], ram_1_dout_2[31], ram_1_dout_2[6:0], ram_1_dout[31], ram_1_dout[6:0]}),
    .in3({StoreValue[7:0], ram_1_dout_3[31], ram_1_dout_3[14:8], ram_1_dout_2[31], ram_1_dout_2[6:0], ram_1_dout[31], ram_1_dout[6:0]}),
    .out(multiplexer_3_out), .sel(subtractor_1_out_2));
  Multiplexer #(.width(32)) multiplexer_4 (
    .in0(StoreValue), .in1(multiplexer_5_out), .out(multiplexer_4_out), .sel(not_1_out));
  not not_1 (not_1_out, Width[1]);
  not not_2 (not_2_out, Width[0]);
  Multiplexer #(.width(32)) multiplexer_5 (
    .in0(multiplexer_2_out), .in1(multiplexer_3_out), .out(multiplexer_5_out), .sel(not_2_out));
  RAM #(.addrWidth(24), .asyncread("true"), .dataWidth(32), .trigger("falling")) ram_1 (
    .addr(subtractor_1_out[25:2]), .we(Store), .oe(or_1_out), .clk(Clock), .din(multiplexer_4_out),
    .dout({ram_1_dout_4[31], ram_1_dout_4[14:8], ram_1_dout_3[31], ram_1_dout_3[14:8], ram_1_dout_2[31], ram_1_dout_2[6:0], ram_1_dout[31], ram_1_dout[6:0]}));
  Multiplexer #(.width(32)) multiplexer_6 (
    .in0({ram_1_dout_4[31], ram_1_dout_4[14:8], ram_1_dout_3[31], ram_1_dout_3[14:8], ram_1_dout_2[31], ram_1_dout_2[6:0], ram_1_dout[31], ram_1_dout[6:0]}),
    .in1(multiplexer_8_out), .out(LoadValue), .sel(not_3_out));
  not not_3 (not_3_out, Width[1]);
  not not_4 (not_4_out, Width[0]);
  Multiplexer #(.width(32)) multiplexer_7 (
    .in0({{17{ram_1_dout_2[31]}}, ram_1_dout_2[6:0], ram_1_dout[31], ram_1_dout[6:0]}),
    .in1({{17{ram_1_dout_3[31]}}, ram_1_dout_3[14:8], ram_1_dout_2[31], ram_1_dout_2[6:0]}),
    .out(multiplexer_7_out), .sel(subtractor_1_out_2[0]));
  Multiplexer #(.width(32)) multiplexer_8 (
    .in0(multiplexer_11_out), .in1(multiplexer_12_out), .out(multiplexer_8_out), .sel(not_4_out));
  Multiplexer #(.width(32)) multiplexer_9 (
    .in0(multiplexer_7_out),
    .in1({{17{ram_1_dout_4[31]}}, ram_1_dout_4[14:8], ram_1_dout_3[31], ram_1_dout_3[14:8]}),
    .out(multiplexer_9_out), .sel(subtractor_1_out_2[1]));
  Multiplexer #(.select(2), .width(32)) multiplexer_10 (
    .in0({{25{ram_1_dout[31]}}, ram_1_dout[6:0]}), .in1({{25{ram_1_dout_2[31]}}, ram_1_dout_2[6:0]}),
    .in2({{25{ram_1_dout_3[31]}}, ram_1_dout_3[14:8]}), .in3({{25{ram_1_dout_4[31]}}, ram_1_dout_4[14:8]}),
    .out(multiplexer_10_out), .sel(subtractor_1_out_2));
  Multiplexer #(.width(32)) multiplexer_11 (
    .in0(multiplexer_9_out), .in1({{16{1'b0}}, multiplexer_9_out[15:0]}), .out(multiplexer_11_out),
    .sel(Width[2]));
  Multiplexer #(.width(32)) multiplexer_12 (
    .in0(multiplexer_10_out), .in1({{24{1'b0}}, multiplexer_10_out[7:0]}), .out(multiplexer_12_out),
    .sel(Width[2]));
endmodule

module IF_ID_Register (
  input  [31:0] Instruction_in,
  input  [31:0] PC_in,
  input  [31:0] PCPlus4_in,
  input  Flush,
  input  Clock,
  input  Rest,
  output [31:0] Instruction_out,
  output [31:0] PC_out,
  output [31:0] PCPlus4_out
);

  wire [31:0] multiplexer_1_out;

  Multiplexer #(.width(32)) multiplexer_1 (.in0(Instruction_in), .in1(32'h13), .out(multiplexer_1_out), .sel(Flush));
  Register #(.trigger("falling"), .width(32)) register_1 (
    .D(multiplexer_1_out), .en(1'b1), .clk(Clock), .Q(Instruction_out), .clr(Rest));
  Register #(.trigger("falling"), .width(32)) register_2 (.D(PC_in), .en(1'b1), .clk(Clock), .Q(PC_out), .clr(Rest));
  Register #(.trigger("falling"), .width(32)) register_3 (
    .D(PCPlus4_in), .en(1'b1), .clk(Clock), .Q(PCPlus4_out), .clr(Rest));
endmodule

module ID_EX_Register_Data (
  input  [31:0] Out1_in,
  input  [31:0] Out2_in,
  input  [31:0] immediate_in,
  input  [31:0] PC_in,
  input  [2:0] Funct3_in,
  input  [6:0] Funct7_in,
  input  [4:0] RD_in,
  input  [31:0] PCPlus4_in,
  input  Rest,
  input  Clock,
  output [31:0] Out1_out,
  output [31:0] Out2_out,
  output [31:0] immediate_out,
  output [31:0] PC_out,
  output [2:0] Funct3_out,
  output [6:0] Funct7_out,
  output [4:0] RD_out,
  output [31:0] PCPlus4_out
);

  Register #(.width(32)) register_1 (.D(Out2_in), .en(1'b1), .clk(Clock), .Q(Out2_out), .clr(Rest));
  Register #(.trigger("falling"), .width(32)) register_2 (
    .D(immediate_in), .en(1'b1), .clk(Clock), .Q(immediate_out), .clr(Rest));
  Register #(.width(32)) register_3 (.D(Out1_in), .en(1'b1), .clk(Clock), .Q(Out1_out), .clr(Rest));
  Register #(.trigger("falling"), .width(32)) register_4 (.D(PC_in), .en(1'b1), .clk(Clock), .Q(PC_out), .clr(Rest));
  Register #(.trigger("falling"), .width(3)) register_5 (
    .D(Funct3_in), .en(1'b1), .clk(Clock), .Q(Funct3_out), .clr(Rest));
  Register #(.trigger("falling"), .width(7)) register_6 (
    .D(Funct7_in), .en(1'b1), .clk(Clock), .Q(Funct7_out), .clr(Rest));
  Register #(.trigger("falling"), .width(5)) register_7 (.D(RD_in), .en(1'b1), .clk(Clock), .Q(RD_out), .clr(Rest));
  Register #(.trigger("falling"), .width(32)) register_8 (
    .D(PCPlus4_in), .en(1'b1), .clk(Clock), .Q(PCPlus4_out), .clr(Rest));

  // Notes on the sheet:
  //   RD_in: initial=0x1
  //   Funct3_in: initial=0x2
  //   immediate_in: initial=0x64
  //   Out1_in: initial=0xa
  //   Out2_in: initial=0x14
  //   PC_in: initial=0x190
  //   Funct7_in: initial=0x20
endmodule

module ID_EX_Register_Control (
  input  Load_in,
  input  Store_in,
  input  ALUResult_Enable_in,
  input  Write_in,
  input  immediate_Enable_in,
  input  ALUSrc_in,
  input  AUIPC_in,
  input  RJump1_in,
  input  RJump2_in,
  input  StorePC_in,
  input  PCSrc_in,
  input  Rest,
  input  Clock,
  input  Flush,
  output Load_out,
  output Store_out,
  output ALUResult_Enable_out,
  output Write_out,
  output immediate_Enab_out,
  output ALUSrc_out,
  output AUIPC_out,
  output RJump1_out,
  output RJump2_out,
  output StorePC_out,
  output PCSrc_out
);

  wire and_1_out, and_2_out, and_3_out, and_4_out, and_5_out, and_6_out, and_7_out, and_8_out, and_9_out,
       and_10_out, and_11_out, not_1_out;

  not not_1 (not_1_out, Flush);
  and and_1 (and_1_out, Load_in, not_1_out);
  and and_2 (and_2_out, Store_in, not_1_out);
  and and_3 (and_3_out, ALUResult_Enable_in, not_1_out);
  and and_4 (and_4_out, Write_in, not_1_out);
  and and_5 (and_5_out, immediate_Enable_in, not_1_out);
  and and_6 (and_6_out, ALUSrc_in, not_1_out);
  and and_7 (and_7_out, AUIPC_in, not_1_out);
  and and_8 (and_8_out, RJump1_in, not_1_out);
  and and_9 (and_9_out, RJump2_in, not_1_out);
  and and_10 (and_10_out, StorePC_in, not_1_out);
  and and_11 (and_11_out, PCSrc_in, not_1_out);
  Register #(.trigger("falling"), .width(1)) register_1 (
    .D(and_1_out), .en(1'b1), .clk(Clock), .Q(Load_out), .clr(Rest));
  Register #(.trigger("falling"), .width(1)) register_2 (
    .D(and_2_out), .en(1'b1), .clk(Clock), .Q(Store_out), .clr(Rest));
  Register #(.trigger("falling"), .width(1)) register_3 (
    .D(and_3_out), .en(1'b1), .clk(Clock), .Q(ALUResult_Enable_out), .clr(Rest));
  Register #(.trigger("falling"), .width(1)) register_4 (
    .D(and_4_out), .en(1'b1), .clk(Clock), .Q(Write_out), .clr(Rest));
  Register #(.trigger("falling"), .width(1)) register_5 (
    .D(and_5_out), .en(1'b1), .clk(Clock), .Q(immediate_Enab_out), .clr(Rest));
  Register #(.trigger("falling"), .width(1)) register_6 (
    .D(and_6_out), .en(1'b1), .clk(Clock), .Q(ALUSrc_out), .clr(Rest));
  Register #(.trigger("falling"), .width(1)) register_7 (
    .D(and_7_out), .en(1'b1), .clk(Clock), .Q(AUIPC_out), .clr(Rest));
  Register #(.trigger("falling"), .width(1)) register_8 (
    .D(and_8_out), .en(1'b1), .clk(Clock), .Q(RJump1_out), .clr(Rest));
  Register #(.trigger("falling"), .width(1)) register_9 (
    .D(and_9_out), .en(1'b1), .clk(Clock), .Q(RJump2_out), .clr(Rest));
  Register #(.trigger("falling"), .width(1)) register_10 (
    .D(and_10_out), .en(1'b1), .clk(Clock), .Q(StorePC_out), .clr(Rest));
  Register #(.trigger("falling"), .width(1)) register_11 (
    .D(and_11_out), .en(1'b1), .clk(Clock), .Q(PCSrc_out), .clr(Rest));

  // Notes on the sheet:
  //   Store_in: initial=0x1
  //   Load_in: initial=0x1
  //   ALUResult_Enable_in: initial=0x1
  //   PCSrc_in: initial=0x1
  //   Write_in: initial=0x1
  //   immediate_Enable_in: initial=0x1
  //   ALUSrc_in: initial=0x1
  //   AUIPC_in: initial=0x1
  //   RJump2_in: initial=0x1
  //   StorePC_in: initial=0x1
  //   RJump1_in: initial=0x1
endmodule

module EX_MEM_Register_Data (
  input  [2:0] MemWidth_in,
  input  [31:0] immediate_in,
  input  [31:0] MemAddr_in,
  input  [31:0] StoreValue_in,
  input  [31:0] ALUResult_in,
  input  [31:0] PCPlus4_in,
  input  [31:0] AUIPC_Result_in,
  input  [4:0] RD_in,
  input  Clock,
  input  Rest,
  output [2:0] MemWidth_out,
  output [31:0] immediate_out,
  output [31:0] MemAddr_out,
  output [31:0] StoreValue_out,
  output [31:0] ALUResult_out,
  output [31:0] PCPlus4_out,
  output [31:0] AUIPC_Result_out,
  output [4:0] RD_out
);

  Register #(.trigger("falling"), .width(3)) register_1 (
    .D(MemWidth_in), .en(1'b1), .clk(Clock), .Q(MemWidth_out), .clr(Rest));
  Register #(.trigger("falling"), .width(32)) register_2 (
    .D(immediate_in), .en(1'b1), .clk(Clock), .Q(immediate_out), .clr(Rest));
  Register #(.trigger("falling"), .width(32)) register_3 (
    .D(MemAddr_in), .en(1'b1), .clk(Clock), .Q(MemAddr_out), .clr(Rest));
  Register #(.trigger("falling"), .width(32)) register_4 (
    .D(StoreValue_in), .en(1'b1), .clk(Clock), .Q(StoreValue_out), .clr(Rest));
  Register #(.trigger("falling"), .width(32)) register_5 (
    .D(ALUResult_in), .en(1'b1), .clk(Clock), .Q(ALUResult_out), .clr(Rest));
  Register #(.trigger("falling"), .width(32)) register_6 (
    .D(PCPlus4_in), .en(1'b1), .clk(Clock), .Q(PCPlus4_out), .clr(Rest));
  Register #(.trigger("falling"), .width(32)) register_7 (
    .D(AUIPC_Result_in), .en(1'b1), .clk(Clock), .Q(AUIPC_Result_out), .clr(Rest));
  Register #(.trigger("falling"), .width(5)) register_8 (.D(RD_in), .en(1'b1), .clk(Clock), .Q(RD_out), .clr(Rest));

  // Notes on the sheet:
  //   MemWidth_in: initial=0x1
  //   RD_in: initial=0x1
  //   MemAddr_in: initial=0x1
  //   StoreValue_in: initial=0x1
  //   ALUResult_in: initial=0x1
  //   PCPlus4_in: initial=0x1
  //   AUIPC_Result_in: initial=0x1
endmodule

module MEM_WB_Register_Data (
  input  [31:0] LoadValue_in,
  input  [4:0] RD_in,
  input  [31:0] immediate_in,
  input  [31:0] ALUResult_in,
  input  [31:0] PCPluse4_in,
  input  [31:0] AUIPC_Result_in,
  input  Rest,
  input  Clock,
  output [31:0] LoadValue_out,
  output [4:0] RD_out,
  output [31:0] immediate_out,
  output [31:0] ALUResult_out,
  output [31:0] PCPluse4_out,
  output [31:0] AUIPC_Result_out
);

  Register #(.trigger("falling"), .width(32)) register_1 (
    .D(LoadValue_in), .en(1'b1), .clk(Clock), .Q(LoadValue_out), .clr(Rest));
  Register #(.trigger("falling"), .width(5)) register_2 (.D(RD_in), .en(1'b1), .clk(Clock), .Q(RD_out), .clr(Rest));
  Register #(.trigger("falling"), .width(32)) register_3 (
    .D(immediate_in), .en(1'b1), .clk(Clock), .Q(immediate_out), .clr(Rest));
  Register #(.trigger("falling"), .width(32)) register_4 (
    .D(ALUResult_in), .en(1'b1), .clk(Clock), .Q(ALUResult_out), .clr(Rest));
  Register #(.trigger("falling"), .width(32)) register_5 (
    .D(PCPluse4_in), .en(1'b1), .clk(Clock), .Q(PCPluse4_out), .clr(Rest));
  Register #(.trigger("falling"), .width(32)) register_6 (
    .D(AUIPC_Result_in), .en(1'b1), .clk(Clock), .Q(AUIPC_Result_out), .clr(Rest));

  // Notes on the sheet:
  //   RD_in: initial=0x2
  //   LoadValue_in: initial=0x2
  //   immediate_in: initial=0x1
  //   AUIPC_Result_in: initial=0x1
  //   ALUResult_in: initial=0x2
  //   PCPluse4_in: initial=0x1
endmodule

module EX_MEM_Register_Control (
  input  Store_in,
  input  Load_in,
  input  ALUResult_Enable_in,
  input  AUIPC_in,
  input  StorePC_in,
  input  Write_in,
  input  immediate_Enable_in,
  input  Clock,
  input  Rest,
  output Store_out,
  output Load_out,
  output ALUResult_Enable_out,
  output AUIPC_out,
  output StorePC_out,
  output Write_out,
  output immediate_Enab_out
);

  Register #(.trigger("falling"), .width(1)) register_1 (
    .D(StorePC_in), .en(1'b1), .clk(Clock), .Q(StorePC_out), .clr(Rest));
  Register #(.trigger("falling"), .width(1)) register_2 (
    .D(Store_in), .en(1'b1), .clk(Clock), .Q(Store_out), .clr(Rest));
  Register #(.trigger("falling"), .width(1)) register_3 (.D(Load_in), .en(1'b1), .clk(Clock), .Q(Load_out), .clr(Rest));
  Register #(.trigger("falling"), .width(1)) register_4 (
    .D(ALUResult_Enable_in), .en(1'b1), .clk(Clock), .Q(ALUResult_Enable_out), .clr(Rest));
  Register #(.trigger("falling"), .width(1)) register_5 (
    .D(AUIPC_in), .en(1'b1), .clk(Clock), .Q(AUIPC_out), .clr(Rest));
  Register #(.trigger("falling"), .width(1)) register_6 (
    .D(Write_in), .en(1'b1), .clk(Clock), .Q(Write_out), .clr(Rest));
  Register #(.trigger("falling"), .width(1)) register_7 (
    .D(immediate_Enable_in), .en(1'b1), .clk(Clock), .Q(immediate_Enab_out), .clr(Rest));

  // Notes on the sheet:
  //   StorePC_in: initial=0x1
  //   Write_in: initial=0x1
  //   immediate_Enable_in: initial=0x1
  //   Store_in: initial=0x1
  //   Load_in: initial=0x1
  //   ALUResult_Enable_in: initial=0x1
  //   AUIPC_in: initial=0x1
endmodule

module MEM_WB_Register_Control (
  input  ALUResult_Enable_in,
  input  Write_in,
  input  immediate_Enab_in,
  input  AUIPC_in,
  input  Load_in,
  input  StorePC_in,
  input  Clock,
  input  Rest,
  output ALUResult_Enable_out,
  output Write_out,
  output immediate_Enab_out,
  output AUIPC_out,
  output Load_out,
  output StorePc_out
);

  Register #(.trigger("falling"), .width(1)) register_1 (
    .D(ALUResult_Enable_in), .en(1'b1), .clk(Clock), .Q(ALUResult_Enable_out), .clr(Rest));
  Register #(.trigger("falling"), .width(1)) register_2 (
    .D(Write_in), .en(1'b1), .clk(Clock), .Q(Write_out), .clr(Rest));
  Register #(.trigger("falling"), .width(1)) register_3 (
    .D(immediate_Enab_in), .en(1'b1), .clk(Clock), .Q(immediate_Enab_out), .clr(Rest));
  Register #(.trigger("falling"), .width(1)) register_4 (
    .D(AUIPC_in), .en(1'b1), .clk(Clock), .Q(AUIPC_out), .clr(Rest));
  Register #(.trigger("falling"), .width(1)) register_5 (.D(Load_in), .en(1'b1), .clk(Clock), .Q(Load_out), .clr(Rest));
  Register #(.trigger("falling"), .width(1)) register_6 (
    .D(StorePC_in), .en(1'b1), .clk(Clock), .Q(StorePc_out), .clr(Rest));

  // Notes on the sheet:
  //   Write_in: initial=0x1
  //   AUIPC_in: initial=0x1
  //   StorePC_in: initial=0x1
endmodule

module Forwarding_Unit (
  input  [4:0] Rs1,
  input  [31:0] Out1_in,
  input  [4:0] EXMEM_RD,
  input  EXMEM_Write,
  input  [4:0] MEMWB_RD,
  input  MEMWB_Write,
  input  [4:0] Rs2,
  input  [31:0] Out2_in,
  input  [31:0] EXMEM_Result,
  input  [31:0] MEMWB_Result,
  output [31:0] A,
  output [31:0] B
);

  wire and_1_out, and_2_out, and_3_out, and_4_out, comparator_1_eq, comparator_2_eq, comparator_3_eq,
       comparator_4_eq, comparator_5_eq, comparator_6_eq, not_1_out, not_2_out;
  wire [31:0] multiplexer_1_out, multiplexer_2_out;

  Comparator #(.mode("unsigned"), .width(5)) comparator_1 (
    .a(Rs1), .b(EXMEM_RD), .eq(comparator_1_eq));  // open: gt, lt
  Comparator #(.mode("unsigned"), .width(5)) comparator_2 (
    .a(Rs1), .b(MEMWB_RD), .eq(comparator_2_eq));  // open: gt, lt
  Comparator #(.mode("unsigned"), .width(5)) comparator_3 (
    .a(Rs2), .b(EXMEM_RD), .eq(comparator_3_eq));  // open: gt, lt
  Comparator #(.mode("unsigned"), .width(5)) comparator_4 (
    .a(Rs2), .b(MEMWB_RD), .eq(comparator_4_eq));  // open: gt, lt
  Comparator #(.mode("unsigned"), .width(5)) comparator_5 (
    .a(EXMEM_RD), .b({5{1'b0}}), .eq(comparator_5_eq));  // open: gt, lt
  Comparator #(.mode("unsigned"), .width(5)) comparator_6 (
    .a(MEMWB_RD), .b({5{1'b0}}), .eq(comparator_6_eq));  // open: gt, lt
  not not_1 (not_1_out, comparator_5_eq);
  not not_2 (not_2_out, comparator_6_eq);
  and and_1 (and_1_out, comparator_1_eq, not_1_out, EXMEM_Write);
  and and_2 (and_2_out, comparator_2_eq, not_2_out, MEMWB_Write);
  and and_3 (and_3_out, comparator_3_eq, not_1_out, EXMEM_Write);
  and and_4 (and_4_out, comparator_4_eq, not_2_out, MEMWB_Write);
  Multiplexer #(.width(32)) multiplexer_1 (.in0(Out2_in), .in1(MEMWB_Result), .out(multiplexer_1_out), .sel(and_4_out));
  Multiplexer #(.width(32)) multiplexer_2 (.in0(Out1_in), .in1(MEMWB_Result), .out(multiplexer_2_out), .sel(and_2_out));
  Multiplexer #(.width(32)) multiplexer_3 (.in0(multiplexer_2_out), .in1(EXMEM_Result), .out(A), .sel(and_1_out));
  Multiplexer #(.width(32)) multiplexer_4 (.in0(multiplexer_1_out), .in1(EXMEM_Result), .out(B), .sel(and_3_out));

  // Notes on the sheet:
  //   EXMEM_RD: initial=0x3
  //   Rs1: initial=0x3
  //   MEMWB_RD: initial=0x2
  //   Rs2: initial=0x1
  //   MEMWB_Result: initial=0x14
  //   EXMEM_Result: initial=0x1e
  //   MEMWB_Write: initial=0x1
  //   EXMEM_Write: initial=0x1
  //   Out2_in: initial=0xa
endmodule

module ID_EX_Data (
  input  [4:0] RS1_in,
  input  [4:0] RS2_in,
  input  Clock,
  input  Rest,
  output [4:0] RS1_out,
  output [4:0] RS2_out
);

  Register #(.trigger("falling"), .width(5)) register_1 (.D(RS1_in), .en(1'b1), .clk(Clock), .Q(RS1_out), .clr(Rest));
  Register #(.trigger("falling"), .width(5)) register_2 (.D(RS2_in), .en(1'b1), .clk(Clock), .Q(RS2_out), .clr(Rest));

  // Notes on the sheet:
  //   RS1_in: initial=0x1
  //   RS2_in: initial=0x1
endmodule
